# Fritzing sketch Project 2 (saved by Fritzing 0.9.3b)

parts:
  Raspberry_Pi_1 = Raspberry Pi 3 [part_number=RPI-3-V1.2]  # not connected
  U1 = Explorer HAT Pro [part_number="Explorer HAT Pro" package=THT]
  Part1 = Thumb Joystick
  Part2 = Thumb Joystick
  M1 = DC Motor
  M2 = DC Motor

nets:
  VCC: U1.5v, Part1.VCC, Part2.VCC
  N1: U1.Analog_1, Part2.VERT
  N2: U1.Analog_2, Part1.VERT
  GND: U1.Ground, Part1.GND, Part2.GND
  N3: U1.Motor_1-, M1.pin_2
  N4: U1.Motor_1+, M1.pin_1
  N5: U1.Motor_2-, M2.pin_2
  N6: U1.Motor_2+, M2.pin_1

custom parts:
  Explorer HAT Pro: Explorer HAT Pro with 4 Output and 4 Input connections, 4 Analog Inputs and 2 bi-directional motor channels, plus power and ground.
